# Fritzing sketch schéma (saved by Fritzing 0.8.3b)
circuit board: 8.37328cm x 7.86314cm
breadboards: 3

parts:
  J1 = female pin header, 28 pins [form="♀ (female)"]
  µContrôlleur = female pin header, 28 pins [form="♀ (female)"]
  Gyroscope = female pin header, 8 pins [form="♀ (female)"]
  Convertisseur_USB/Série = female pin header, 5 pins [form="♀ (female)"]
  Altimètre = female pin header, 5 pins [form="♀ (female)"]
  JP1 = Header 5x2 [package=2x5-shrouded_smd]
  R3 = Resistor [tolerance=±5% resistance=4.7k package="1206 [SMD]"]
  R4 = Resistor [tolerance=±5% resistance=4.7k package="1206 [SMD]"]
  TLV117 = NPN-Transistor [package="TO92 [THT]"]
  Jumper_activation_vidéo = female pin header, 2 pins [form="♀ (female)"]

nets:
  N1: J1.pin2, J1.pin28, Convertisseur_USB/Série.pin5, JP1.1, JP1.2, JP1.3, JP1.4, JP1.7, JP1.8, TLV117.E, TLV117.C, Jumper_activation_vidéo.pin1, Jumper_activation_vidéo.pin2
  N2: J1.pin3, Convertisseur_USB/Série.pin2, TLV117.B
  N3: J1.pin17, Convertisseur_USB/Série.pin3
  N4: J1.pin18, Convertisseur_USB/Série.pin4
  N5: J1.pin23, J1.pin24, JP1.5, JP1.6
  N6: µContrôlleur.pin2, µContrôlleur.pin5, µContrôlleur.pin28, Gyroscope.pin2, Gyroscope.pin7, Altimètre.pin3
  N7: µContrôlleur.pin7, Gyroscope.pin4, Altimètre.pin5, R3.Pin_1
  N8: µContrôlleur.pin8, Gyroscope.pin3, Altimètre.pin4, R4.Pin_1
  N9: Gyroscope.pin1, Altimètre.pin2, R3.Pin_0, R4.Pin_0
  N10: JP1.9, JP1.10
